// Digital circuit FullAdderRCSig.dig as structural Verilog
// 4-bit ripple carry adder, consisting of four full adders.
// {{de 4-Bit Ripple-Carry addierer bestehend aus vier 
// Volladdierern.}}
module FullAdderRCSig (
  input  C__1,
  input  A_0,
  input  B_0,
  input  A_1,
  input  B_1,
  input  A_2,
  input  B_2,
  input  A_3,
  input  B_3,
  output S_0,
  output S_1,
  output S_2,
  output C_3,
  output S_3
);

  wire and_1_out, and_2_out, and_3_out, and_4_out, and_5_out, and_6_out, and_7_out, and_8_out, or_2_out,
       or_3_out, or_4_out, xor_1_out, xor_2_out, xor_3_out, xor_4_out;

  and and_1 (and_1_out, A_3, B_3);
  xor xor_1 (xor_1_out, A_3, B_3);
  and and_2 (and_2_out, A_2, B_2);
  xor xor_2 (xor_2_out, A_2, B_2);
  and and_3 (and_3_out, A_1, B_1);
  xor xor_3 (xor_3_out, A_1, B_1);
  and and_4 (and_4_out, A_0, B_0);
  xor xor_4 (xor_4_out, A_0, B_0);
  and and_5 (and_5_out, xor_1_out, or_2_out);
  xor xor_5 (S_3, xor_1_out, or_2_out);
  and and_6 (and_6_out, xor_2_out, or_3_out);
  xor xor_6 (S_2, xor_2_out, or_3_out);
  and and_7 (and_7_out, xor_3_out, or_4_out);
  xor xor_7 (S_1, xor_3_out, or_4_out);
  and and_8 (and_8_out, xor_4_out, C__1);
  xor xor_8 (S_0, xor_4_out, C__1);
  or or_1 (C_3, and_1_out, and_5_out);
  or or_2 (or_2_out, and_2_out, and_6_out);
  or or_3 (or_3_out, and_3_out, and_7_out);
  or or_4 (or_4_out, and_4_out, and_8_out);

  // Notes on the sheet:
  //   A_0: default 1
  //   B_1: default 1
  //   A_2: default 1
  //   B_3: default 1
endmodule

/* Test case:
# complete test of all 512 possible additions
C_-1 A_3 A_2 A_1 A_0 B_3 B_2 B_1 B_0 C_3 S_3 S_2 S_1 S_0
repeat(256) 0 bits(4,n>>4) bits(4,n) bits(5,(n>>4)+(n&15))
repeat(256) 1 bits(4,n>>4) bits(4,n) bits(5,(n>>4)+(n&15)+1)
*/
