// Digital circuit FullAdderRC_CLA.dig as structural Verilog
// Example to compare RC and CLA adders.
// {{de Beispiel um RC- und CLA-Addierer zu vergleichen.}}
module FullAdderRC_CLA (
  input  C0,
  input  A0,
  input  B0,
  input  A1,
  input  B1,
  input  A2,
  input  B2,
  input  A3,
  input  B3,
  input  A0_2,
  input  B0_2,
  input  C0_2,
  input  A1_2,
  input  B1_2,
  input  A2_2,
  input  B2_2,
  input  A3_2,
  input  B3_2,
  output S0,
  output S1,
  output S2,
  output C3,
  output S3,
  output S0_2,
  output S1_2,
  output S2_2,
  output S3_2,
  output C3_2
);

  wire and_1_out, and_2_out, and_3_out, and_4_out, and_5_out, and_6_out, and_7_out, and_8_out, and_9_out,
       and_10_out, and_11_out, and_12_out, and_13_out, and_14_out, and_15_out, and_16_out, and_17_out,
       and_18_out, and_19_out, and_20_out, and_21_out, and_22_out, or_2_out, or_3_out, or_4_out, or_5_out,
       or_6_out, or_7_out, or_8_out, or_10_out, or_11_out, or_12_out, xor_1_out, xor_2_out, xor_3_out,
       xor_4_out, xor_9_out, xor_10_out, xor_11_out, xor_12_out;

  and and_1 (and_1_out, A3, B3);
  xor xor_1 (xor_1_out, A3, B3);
  and and_2 (and_2_out, A2, B2);
  xor xor_2 (xor_2_out, A2, B2);
  and and_3 (and_3_out, A1, B1);
  xor xor_3 (xor_3_out, A1, B1);
  and and_4 (and_4_out, A0, B0);
  xor xor_4 (xor_4_out, A0, B0);
  and and_5 (and_5_out, xor_1_out, or_2_out);
  xor xor_5 (S3, xor_1_out, or_2_out);
  and and_6 (and_6_out, xor_2_out, or_3_out);
  xor xor_6 (S2, xor_2_out, or_3_out);
  and and_7 (and_7_out, xor_3_out, or_4_out);
  xor xor_7 (S1, xor_3_out, or_4_out);
  and and_8 (and_8_out, xor_4_out, C0);
  xor xor_8 (S0, xor_4_out, C0);
  or or_1 (C3, and_1_out, and_5_out);
  or or_2 (or_2_out, and_2_out, and_6_out);
  or or_3 (or_3_out, and_3_out, and_7_out);
  or or_4 (or_4_out, and_4_out, and_8_out);
  or or_5 (or_5_out, A3_2, B3_2);
  and and_9 (and_9_out, A3_2, B3_2);
  or or_6 (or_6_out, A2_2, B2_2);
  and and_10 (and_10_out, A2_2, B2_2);
  or or_7 (or_7_out, A1_2, B1_2);
  and and_11 (and_11_out, A1_2, B1_2);
  or or_8 (or_8_out, A0_2, B0_2);
  and and_12 (and_12_out, A0_2, B0_2);
  and and_13 (and_13_out, C0_2, or_8_out, or_7_out, or_6_out, or_5_out);
  and and_14 (and_14_out, and_12_out, or_5_out, or_6_out, or_7_out);
  and and_15 (and_15_out, and_11_out, or_6_out, or_5_out);
  and and_16 (and_16_out, or_5_out, and_10_out);
  xor xor_9 (xor_9_out, or_5_out, and_9_out);
  and and_17 (and_17_out, C0_2, or_8_out, or_7_out, or_6_out);
  and and_18 (and_18_out, or_7_out, or_6_out, and_12_out);
  and and_19 (and_19_out, or_6_out, and_11_out);
  xor xor_10 (xor_10_out, or_6_out, and_10_out);
  and and_20 (and_20_out, C0_2, or_8_out, or_7_out);
  and and_21 (and_21_out, or_7_out, and_12_out);
  xor xor_11 (xor_11_out, or_7_out, and_11_out);
  and and_22 (and_22_out, or_8_out, C0_2);
  xor xor_12 (xor_12_out, or_8_out, and_12_out);
  or or_9 (C3_2, and_13_out, and_14_out, and_15_out, and_16_out, and_9_out);
  or or_10 (or_10_out, and_17_out, and_18_out, and_19_out, and_10_out);
  or or_11 (or_11_out, and_20_out, and_21_out, and_11_out);
  or or_12 (or_12_out, and_22_out, and_12_out);
  xor xor_13 (S2_2, xor_10_out, or_11_out);
  xor xor_14 (S1_2, xor_11_out, or_12_out);
  xor xor_15 (S0_2, xor_12_out, C0_2);
  xor xor_16 (S3_2, xor_9_out, or_10_out);

  // Notes on the sheet:
  //   A0: default 1
  //   B1: default 1
  //   B2: default 1
  //   A3: default 1
  //   A0_2: default 1
  //   B1_2: default 1
  //   B2_2: default 1
  //   A3_2: default 1
endmodule
