// Digital circuit Oscillation.dig as structural Verilog
module Oscillation (
  input  in_1,
  output out_2
);

  wire not_1_out, xor_1_out;

  xor xor_1 (xor_1_out, in_1, out_2);
  not not_1 (not_1_out, xor_1_out);
  not not_2 (out_2, not_1_out);
endmodule
