// Digital circuit 74280.dig as structural Verilog
// 9 bit Odd-Even Parity Generator-Checker
module _74280 (
  input  A,
  input  B,
  input  C,
  input  D,
  input  E,
  input  F,
  input  G,
  input  H,
  input  I,
  input  VCC,
  input  GND,
  output EVEN,
  output ODD
);

  wire and_1_out, and_2_out, and_3_out, and_4_out, and_5_out, and_6_out, and_7_out, and_8_out, and_9_out,
       and_10_out, and_11_out, and_12_out, and_13_out, and_14_out, and_15_out, and_16_out, and_17_out,
       and_18_out, and_19_out, and_20_out, nor_1_out, nor_2_out, nor_3_out, not_1_out, not_2_out, not_3_out,
       not_4_out, not_5_out, not_6_out, not_7_out, not_8_out, not_9_out, not_10_out, not_11_out, not_12_out,
       not_13_out, not_14_out, not_15_out, not_16_out, not_17_out, not_18_out, not_19_out, not_20_out,
       not_21_out;

  not not_1 (not_1_out, A);
  not not_2 (not_2_out, B);
  not not_3 (not_3_out, C);
  not not_4 (not_4_out, D);
  not not_5 (not_5_out, E);
  not not_6 (not_6_out, F);
  not not_7 (not_7_out, G);
  not not_8 (not_8_out, H);
  not not_9 (not_9_out, I);
  not not_10 (not_10_out, not_1_out);
  not not_11 (not_11_out, not_2_out);
  not not_12 (not_12_out, not_3_out);
  not not_13 (not_13_out, not_4_out);
  not not_14 (not_14_out, not_5_out);
  not not_15 (not_15_out, not_6_out);
  not not_16 (not_16_out, not_7_out);
  not not_17 (not_17_out, not_8_out);
  not not_18 (not_18_out, not_9_out);
  and and_1 (and_1_out, not_2_out, not_3_out, not_10_out);
  and and_2 (and_2_out, not_1_out, not_3_out, not_11_out);
  and and_3 (and_3_out, not_2_out, not_1_out, not_12_out);
  and and_4 (and_4_out, not_12_out, not_11_out, not_10_out);
  and and_5 (and_5_out, not_5_out, not_6_out, not_13_out);
  and and_6 (and_6_out, not_4_out, not_6_out, not_14_out);
  and and_7 (and_7_out, not_5_out, not_4_out, not_15_out);
  and and_8 (and_8_out, not_15_out, not_14_out, not_13_out);
  and and_9 (and_9_out, not_8_out, not_9_out, not_16_out);
  and and_10 (and_10_out, not_7_out, not_9_out, not_17_out);
  and and_11 (and_11_out, not_8_out, not_7_out, not_18_out);
  and and_12 (and_12_out, not_18_out, not_17_out, not_16_out);
  nor nor_1 (nor_1_out, and_1_out, and_2_out, and_3_out, and_4_out);
  nor nor_2 (nor_2_out, and_5_out, and_6_out, and_7_out, and_8_out);
  nor nor_3 (nor_3_out, and_9_out, and_10_out, and_11_out, and_12_out);
  not not_19 (not_19_out, nor_1_out);
  not not_20 (not_20_out, nor_2_out);
  not not_21 (not_21_out, nor_3_out);
  and and_13 (and_13_out, nor_2_out, nor_3_out, not_19_out);
  and and_14 (and_14_out, nor_1_out, nor_3_out, not_20_out);
  and and_15 (and_15_out, nor_1_out, nor_2_out, not_21_out);
  and and_16 (and_16_out, not_19_out, not_20_out, not_21_out);
  and and_17 (and_17_out, not_20_out, not_21_out, nor_1_out);
  and and_18 (and_18_out, nor_2_out, not_19_out, not_21_out);
  and and_19 (and_19_out, not_20_out, not_19_out, nor_3_out);
  and and_20 (and_20_out, nor_2_out, nor_1_out, nor_3_out);
  PowerSupply powersupply_1 (.VDD(VCC), .GND(GND));
  nor nor_4 (EVEN, and_13_out, and_14_out, and_15_out, and_16_out);
  nor nor_5 (ODD, and_17_out, and_18_out, and_19_out, and_20_out);

  // Notes on the sheet:
  //   A: pin 8
  //   B: pin 9
  //   C: pin 10
  //   D: pin 11
  //   E: pin 12
  //   F: pin 13
  //   G: pin 1
  //   H: pin 2
  //   I: pin 4
  //   EVEN: pin 5
  //   ODD: pin 6
  //   VCC: pin 14, default 1
  //   GND: pin 7
endmodule

/* Test case:
A B C D E F G H I EVEN ODD

loop (n,256)
  let p=((n&1)^((n>>1)&1)^((n>>2)&1)^((n>>3)&1)^((n>>4)&1)^((n>>5)&1)^((n>>6)&1)^((n>>7)&1)^((n>>8)&1));
  bits(9,n) (~p) (p)
end loop
*/
