// Digital circuit 7403.dig as structural Verilog
// quad 2-input NAND gate with open-collector outputs, different pinout than 7401
module _7403 (
  input  _2A,
  input  _2B,
  input  VCC,
  input  GND,
  input  _3A,
  input  _3B,
  input  _4A,
  input  _4B,
  input  _1A,
  input  _1B,
  output _2Y,
  output _3Y,
  output _4Y,
  output _1Y
);

  wire and_1_out, and_2_out, and_3_out, and_4_out;

  and and_1 (and_1_out, _1A, _1B);
  and and_2 (and_2_out, _2A, _2B);
  and and_3 (and_3_out, _3A, _3B);
  and and_4 (and_4_out, _4A, _4B);
  PowerSupply powersupply_1 (.VDD(VCC), .GND(GND));
  NFET nfet_1 (.G(and_1_out), .D(_1Y), .S(1'b0));
  NFET nfet_2 (.G(and_2_out), .D(_2Y), .S(1'b0));
  NFET nfet_3 (.G(and_3_out), .D(_3Y), .S(1'b0));
  NFET nfet_4 (.G(and_4_out), .D(_4Y), .S(1'b0));

  // Notes on the sheet:
  //   _2A: pin 4
  //   _2B: pin 5
  //   _2Y: pin 6
  //   VCC: pin 14, default 1
  //   GND: pin 7
  //   _3A: pin 9
  //   _3B: pin 10
  //   _3Y: pin 8
  //   _4A: pin 12
  //   _4B: pin 13
  //   _4Y: pin 11
  //   _1A: pin 1
  //   _1B: pin 2
  //   _1Y: pin 3
endmodule
