// Digital circuit 7412.dig as structural Verilog
// triple 3-input NAND gate with open-collector outputs
module _7412 (
  input  _1A,
  input  _1C,
  input  _2A,
  input  _2C,
  input  _3C,
  input  _3A,
  input  _1B,
  input  _2B,
  input  _3B,
  input  VCC,
  input  GND,
  output _1Y,
  output _2Y,
  output _3Y
);

  wire and_1_out, and_2_out, and_3_out;

  and and_1 (and_1_out, _1A, _1B, _1C);
  and and_2 (and_2_out, _2A, _2B, _2C);
  and and_3 (and_3_out, _3A, _3B, _3C);
  PowerSupply powersupply_1 (.VDD(VCC), .GND(GND));
  NFET nfet_1 (.G(and_1_out), .D(_1Y), .S(1'b0));
  NFET nfet_2 (.G(and_2_out), .D(_2Y), .S(1'b0));
  NFET nfet_3 (.G(and_3_out), .D(_3Y), .S(1'b0));

  // Notes on the sheet:
  //   _1A: pin 1
  //   _1C: pin 13
  //   _1Y: pin 12
  //   _2A: pin 3
  //   _2C: pin 5
  //   _2Y: pin 6
  //   _3C: pin 11
  //   _3A: pin 9
  //   _3Y: pin 8
  //   _1B: pin 2
  //   _2B: pin 4
  //   _3B: pin 10
  //   VCC: pin 14, default 1
  //   GND: pin 7
endmodule
