// Digital circuit 74133.dig as structural Verilog
// 13-input NAND gate
module _74133 (
  input  A,
  input  B,
  input  C,
  input  D,
  input  E,
  input  F,
  input  G,
  input  H,
  input  I,
  input  J,
  input  K,
  input  L,
  input  M,
  input  VCC,
  input  GND,
  output Y
);

  nand nand_1 (Y, A, B, C, D, E, F, G, H, I, J, K, L, M);
  PowerSupply powersupply_1 (.VDD(VCC), .GND(GND));

  // Notes on the sheet:
  //   Y: pin 9
  //   A: pin 1
  //   B: pin 2
  //   C: pin 3
  //   D: pin 4
  //   E: pin 5
  //   F: pin 6
  //   G: pin 7
  //   H: pin 10
  //   I: pin 11
  //   J: pin 12
  //   K: pin 13
  //   L: pin 14
  //   M: pin 15
  //   VCC: pin 16, default 1
  //   GND: pin 8
endmodule
