// Digital circuit 7428.dig as structural Verilog
// quad 2-input NOR buffer
module _7428 (
  input  _1A,
  input  _1B,
  input  _2A,
  input  _2B,
  input  _3B,
  input  _3A,
  input  _4A,
  input  _4B,
  input  VCC,
  input  GND,
  output _1Y,
  output _2Y,
  output _3Y,
  output _4Y
);

  nor nor_1 (_1Y, _1A, _1B);
  nor nor_2 (_2Y, _2A, _2B);
  nor nor_3 (_3Y, _3A, _3B);
  nor nor_4 (_4Y, _4A, _4B);
  PowerSupply powersupply_1 (.VDD(VCC), .GND(GND));

  // Notes on the sheet:
  //   _1A: pin 2
  //   _1B: pin 3
  //   _1Y: pin 1
  //   _2A: pin 5
  //   _2B: pin 6
  //   _2Y: pin 4
  //   _3B: pin 9
  //   _3A: pin 8
  //   _3Y: pin 10
  //   _4A: pin 11
  //   _4B: pin 12
  //   _4Y: pin 13
  //   VCC: pin 14, default 1
  //   GND: pin 7
endmodule
