// Digital circuit 7451.dig as structural Verilog
// 2-input/3-input AND-NOR gate
module _7451 (
  input  _1A,
  input  _1C,
  input  _1D,
  input  _1F,
  input  _1B,
  input  _1E,
  input  _2A,
  input  _2B,
  input  _2C,
  input  _2D,
  input  VCC,
  input  GND,
  output _1Q,
  output _2Q
);

  wire and_1_out, and_2_out, and_3_out, and_4_out;

  and and_1 (and_1_out, _1A, _1B, _1C);
  and and_2 (and_2_out, _1D, _1E, _1F);
  and and_3 (and_3_out, _2A, _2B);
  and and_4 (and_4_out, _2C, _2D);
  PowerSupply powersupply_1 (.VDD(VCC), .GND(GND));
  nor nor_1 (_1Q, and_1_out, and_2_out);
  nor nor_2 (_2Q, and_3_out, and_4_out);

  // Notes on the sheet:
  //   _1Q: pin 8
  //   _1A: pin 1
  //   _1C: pin 12
  //   _1D: pin 11
  //   _1F: pin 9
  //   _1B: pin 13
  //   _1E: pin 10
  //   _2Q: pin 6
  //   _2A: pin 2
  //   _2B: pin 3
  //   _2C: pin 4
  //   _2D: pin 5
  //   VCC: pin 14, default 1
  //   GND: pin 7
endmodule
