// Digital circuit 74373-D-inc.dig as structural Verilog
// transparent d latch
module _74373_D_inc (
  input  D,
  input  G,
  output Q
);

  wire and_1_out, and_2_out;

  and and_1 (and_1_out, G, D);
  and and_2 (and_2_out, G, ~D);  // And
  RS_FF_AS rs_ff_as_1 (.S(and_1_out), .R(and_2_out), .Q(Q));  // open: nQ
endmodule
