// Digital circuit 7474.dig as structural Verilog
// dual D-flip-flop
module _7474 (
  input  _1nSD,
  input  _1D,
  input  _1CP,
  input  _1nRD,
  input  _2nSD,
  input  _2D,
  input  _2CP,
  input  _2nRD,
  input  VCC,
  input  GND,
  output _1Q,
  output _1nQ,
  output _2Q,
  output _2nQ
);

  wire and_1_out, and_2_out, d_ff_as_1_nq, d_ff_as_2_nq;

  D_FF_AS d_ff_as_1 (.Set(~_1nSD), .D(_1D), .C(_1CP), .Clr(~_1nRD), .Q(_1Q), .nQ(d_ff_as_1_nq));
  D_FF_AS d_ff_as_2 (.Set(~_2nSD), .D(_2D), .C(_2CP), .Clr(~_2nRD), .Q(_2Q), .nQ(d_ff_as_2_nq));
  PowerSupply powersupply_1 (.VDD(VCC), .GND(GND));
  and and_1 (and_1_out, ~_1nSD, ~_1nRD);  // And
  and and_2 (and_2_out, ~_2nSD, ~_2nRD);  // And
  or or_1 (_1nQ, d_ff_as_1_nq, and_1_out);
  or or_2 (_2nQ, d_ff_as_2_nq, and_2_out);

  // Notes on the sheet:
  //   _1Q: pin 5
  //   _1nQ: pin 6
  //   _1nSD: pin 4
  //   _1D: pin 2
  //   _1CP: pin 3
  //   _1nRD: pin 1
  //   _2Q: pin 9
  //   _2nQ: pin 8
  //   _2nSD: pin 10
  //   _2D: pin 12
  //   _2CP: pin 11
  //   _2nRD: pin 13
  //   VCC: pin 14, default 1
  //   GND: pin 7
endmodule

/* Test case #1:
1~SD 1~RD 1CP 1D 1Q 1~Q
0 1 X X 1 0
1 0 X X 0 1
0 0 X X 1 1

1 1 C 1 1 0
1 1 0 X 1 0

1 1 C 0 0 1
1 1 0 X 0 1
*/

/* Test case #2:
2~SD 2~RD 2CP 2D 2Q 2~Q
0 1 X X 1 0
1 0 X X 0 1
0 0 X X 1 1

1 1 C 1 1 0
1 1 0 X 1 0

1 1 C 0 0 1
1 1 0 X 0 1
*/
