// Digital circuit PAL.dig as structural Verilog
// Simple PAL component with three inputs and two outputs. 
// The component is programmed via the diodes, which can be 
// burned or programmed. For simplicity, the diodes can be 
// programmed with the [P] key.
// {{de Einfacher PAL Baustein mit drei Eingängen und 
// zwei Ausgängen. Programmiert wird der Baustein
// über die Dioden, die "durchgebrannt" bzw. 
// Programmiert werden können. Zur Vereinfachung 
// können die Dioden mit der Taste [P] programmiert 
// werden.}}
module PAL (
  input  A,
  input  B,
  input  C,
  output Y_0,
  output Y_1
);

  wire diodebackward_1_out, diodebackward_3_out, diodebackward_5_out, diodebackward_7_out,
       diodebackward_9_out, diodebackward_11_out, diodebackward_13_out, diodebackward_15_out, not_1_out,
       not_2_out, not_3_out;

  not not_1 (not_1_out, A);
  DiodeBackward diodebackward_1 (.in(A), .out(diodebackward_1_out));
  DiodeBackward #(.Blown("true")) diodebackward_2 (.in(not_1_out), .out(diodebackward_1_out));
  DiodeBackward #(.Blown("true")) diodebackward_3 (.in(A), .out(diodebackward_3_out));
  DiodeBackward diodebackward_4 (.in(not_1_out), .out(diodebackward_3_out));
  DiodeBackward diodebackward_5 (.in(A), .out(diodebackward_5_out));
  DiodeBackward diodebackward_6 (.in(not_1_out), .out(diodebackward_5_out));
  DiodeBackward diodebackward_7 (.in(A), .out(diodebackward_7_out));
  DiodeBackward diodebackward_8 (.in(not_1_out), .out(diodebackward_7_out));
  DiodeBackward diodebackward_9 (.in(A), .out(diodebackward_9_out));
  DiodeBackward #(.Blown("true")) diodebackward_10 (.in(not_1_out), .out(diodebackward_9_out));
  DiodeBackward #(.Blown("true")) diodebackward_11 (.in(A), .out(diodebackward_11_out));
  DiodeBackward diodebackward_12 (.in(not_1_out), .out(diodebackward_11_out));
  DiodeBackward diodebackward_13 (.in(A), .out(diodebackward_13_out));
  DiodeBackward diodebackward_14 (.in(not_1_out), .out(diodebackward_13_out));
  DiodeBackward diodebackward_15 (.in(A), .out(diodebackward_15_out));
  DiodeBackward diodebackward_16 (.in(not_1_out), .out(diodebackward_15_out));
  not not_2 (not_2_out, B);
  DiodeBackward #(.Blown("true")) diodebackward_17 (.in(B), .out(diodebackward_1_out));
  DiodeBackward diodebackward_18 (.in(not_2_out), .out(diodebackward_1_out));
  DiodeBackward diodebackward_19 (.in(B), .out(diodebackward_3_out));
  DiodeBackward #(.Blown("true")) diodebackward_20 (.in(not_2_out), .out(diodebackward_3_out));
  DiodeBackward diodebackward_21 (.in(B), .out(diodebackward_5_out));
  DiodeBackward diodebackward_22 (.in(not_2_out), .out(diodebackward_5_out));
  DiodeBackward diodebackward_23 (.in(B), .out(diodebackward_7_out));
  DiodeBackward diodebackward_24 (.in(not_2_out), .out(diodebackward_7_out));
  DiodeBackward diodebackward_25 (.in(B), .out(diodebackward_9_out));
  DiodeBackward #(.Blown("true")) diodebackward_26 (.in(not_2_out), .out(diodebackward_9_out));
  DiodeBackward #(.Blown("true")) diodebackward_27 (.in(B), .out(diodebackward_11_out));
  DiodeBackward diodebackward_28 (.in(not_2_out), .out(diodebackward_11_out));
  DiodeBackward diodebackward_29 (.in(B), .out(diodebackward_13_out));
  DiodeBackward diodebackward_30 (.in(not_2_out), .out(diodebackward_13_out));
  DiodeBackward diodebackward_31 (.in(B), .out(diodebackward_15_out));
  DiodeBackward diodebackward_32 (.in(not_2_out), .out(diodebackward_15_out));
  not not_3 (not_3_out, C);
  DiodeBackward #(.Blown("true")) diodebackward_33 (.in(C), .out(diodebackward_1_out));
  DiodeBackward #(.Blown("true")) diodebackward_34 (.in(not_3_out), .out(diodebackward_1_out));
  DiodeBackward #(.Blown("true")) diodebackward_35 (.in(C), .out(diodebackward_3_out));
  DiodeBackward #(.Blown("true")) diodebackward_36 (.in(not_3_out), .out(diodebackward_3_out));
  DiodeBackward diodebackward_37 (.in(C), .out(diodebackward_5_out));
  DiodeBackward diodebackward_38 (.in(not_3_out), .out(diodebackward_5_out));
  DiodeBackward diodebackward_39 (.in(C), .out(diodebackward_7_out));
  DiodeBackward diodebackward_40 (.in(not_3_out), .out(diodebackward_7_out));
  DiodeBackward #(.Blown("true")) diodebackward_41 (.in(C), .out(diodebackward_9_out));
  DiodeBackward #(.Blown("true")) diodebackward_42 (.in(not_3_out), .out(diodebackward_9_out));
  DiodeBackward #(.Blown("true")) diodebackward_43 (.in(C), .out(diodebackward_11_out));
  DiodeBackward #(.Blown("true")) diodebackward_44 (.in(not_3_out), .out(diodebackward_11_out));
  DiodeBackward diodebackward_45 (.in(C), .out(diodebackward_13_out));
  DiodeBackward diodebackward_46 (.in(not_3_out), .out(diodebackward_13_out));
  DiodeBackward diodebackward_47 (.in(C), .out(diodebackward_15_out));
  DiodeBackward diodebackward_48 (.in(not_3_out), .out(diodebackward_15_out));
  PullUp pullup_1 (.out(diodebackward_1_out));
  PullUp pullup_2 (.out(diodebackward_3_out));
  or or_1 (Y_0, diodebackward_1_out, diodebackward_3_out, diodebackward_5_out, diodebackward_7_out);
  PullUp pullup_3 (.out(diodebackward_5_out));
  PullUp pullup_4 (.out(diodebackward_7_out));
  PullUp pullup_5 (.out(diodebackward_9_out));
  PullUp pullup_6 (.out(diodebackward_11_out));
  or or_2 (Y_1, diodebackward_9_out, diodebackward_11_out, diodebackward_13_out, diodebackward_15_out);
  PullUp pullup_7 (.out(diodebackward_13_out));
  PullUp pullup_8 (.out(diodebackward_15_out));

  // Notes on the sheet:
  //   A: First freely configurable input.
  //   {{de Erster frei konfigurierbarer Eingang.}}
  //   B: Second freely configurable input.
  //   {{de Zweiter frei konfigurierbarer Eingang.}}
  //   C: Third freely configurable input.
  //   {{de Dritter frei Konfigurierbarer Eingang.}}
  //   Y_0: The output bit 0.
  //   {{de Das 0. Ausgangsbit.}}
  //   Y_1: The output bit 1.
  //   {{de Das 1. Ausgangsbit.}}
endmodule

/* Test case Y_0=A xor B:
A B C Y_0
0 0 x  0
0 1 x  1  
1 0 x  1  
1 1 x  0  
*/

/* Test case Y_1=A xor !B:
A B C Y_1
0 0 x  1  
0 1 x  0  
1 0 x  0  
1 1 x  1  
*/
