// Digital circuit Rising.dig as structural Verilog
// A block for asynchronous storage.
// As soon as the set input goes to 1, the output 
// is switched to 1. The output does not return 
// to 0 until Reset is set to 1.
// {{de Ein Baustein zum asynchronen Speichern.
// Sobald der Set Eingang auf 1 geht, wird der 
// Ausgang auf 1 geschaltet. Der Ausgang geht 
// erst wieder auf 0 zurück, wenn Reset auf 1 
// gesetzt wird.}}
module Rising (
  input  Reset,
  input  Set,
  output Out
);

  wire not_1_out, or_1_out;

  or or_1 (or_1_out, Set, Out);
  not not_1 (not_1_out, Reset);
  and and_1 (Out, or_1_out, not_1_out);

  // Notes on the sheet:
  //   Reset: Sets the output back to zero.
  //   {{de Setzt den Ausgang zurück auf 0.}}
  //   Set: Sets the output to 1.
  //   {{de Setzt den Ausgang auf 1.}}
  //   Out: Switches to high as soon as the Set input goes to high.
  //   {{de Wechselt auf 1 sobald Set auf 1 wechselt.}}
endmodule
