// Digital circuit D-T.dig as structural Verilog
module D_T (
  input  D,
  input  C,
  output Q,
  output nQ
);

  wire and_1_out, and_2_out, and_3_out, delay_1_out, not_1_out, not_2_out;

  not not_1 (not_1_out, C);
  not not_2 (not_2_out, D);
  and and_1 (and_1_out, delay_1_out, C);
  Delay delay_1 (.in(not_1_out), .out(delay_1_out));
  and and_2 (and_2_out, not_2_out, and_1_out);
  and and_3 (and_3_out, and_1_out, D);
  nor nor_1 (Q, and_2_out, nQ);
  nor nor_2 (nQ, Q, and_3_out);
endmodule

/* Test case:
C D Q ~Q
C 1 1  0
0 1 1  0
0 0 1  0
C 0 0  1
0 0 0  1
0 1 0  1
*/
