// Digital circuit D-TransmissionGate.dig as structural Verilog
module D_TransmissionGate (
  input  D,
  input  C,
  output Q,
  output nQ
);

  wire not_1_out, transgate_2_out2;

  not not_1 (not_1_out, C);
  TransGate transgate_1 (.A(C), .nA(not_1_out), .out1(Q), .out2(D));
  TransGate transgate_2 (.A(not_1_out), .nA(C), .out1(Q), .out2(transgate_2_out2));
  not not_2 (nQ, Q);
  not not_3 (transgate_2_out2, nQ);
endmodule

/* Test case:
C D Q ~Q
C 1 1  0
0 1 1  0
0 0 1  0
C 0 0  1
0 0 0  1
0 1 0  1
C 1 1  0
C 0 0  1
*/
