// Digital circuit D.dig as structural Verilog
module D (
  input  D,
  input  C,
  output Q,
  output nQ
);

  wire and_1_out, and_2_out, not_1_out;

  not not_1 (not_1_out, D);
  and and_1 (and_1_out, not_1_out, C);
  and and_2 (and_2_out, C, D);
  nor nor_1 (Q, and_1_out, nQ);
  nor nor_2 (nQ, Q, and_2_out);
endmodule

/* Test case:
C D Q ~Q
C 1 1  0
0 1 1  0
0 0 1  0
C 0 0  1
0 0 0  1
0 1 0  1
*/
