// Digital circuit RS-MS.dig as structural Verilog
module RS_MS (
  input  S,
  input  C,
  input  R,
  output Q,
  output nQ
);

  wire and_1_out, and_2_out, and_3_out, and_4_out, nor_1_out, nor_2_out, not_1_out;

  and and_1 (and_1_out, S, C);
  and and_2 (and_2_out, C, R);
  not not_1 (not_1_out, C);
  nor nor_1 (nor_1_out, and_1_out, nor_2_out);
  nor nor_2 (nor_2_out, nor_1_out, and_2_out);
  and and_3 (and_3_out, nor_1_out, not_1_out);
  and and_4 (and_4_out, not_1_out, nor_2_out);
  nor nor_3 (Q, and_3_out, nQ);
  nor nor_4 (nQ, Q, and_4_out);
endmodule

/* Test case:
R C S Q ~Q
1 C 0 0  1
X 0 X 0  1
0 C 1 1  0
X 0 X 1  0
*/
