// Digital circuit RS.dig as structural Verilog
module RS (
  input  R,
  input  S,
  output Q,
  output nQ
);

  nor nor_1 (Q, R, nQ);
  nor nor_2 (nQ, Q, S);
endmodule

/* Test case:
R S Q ~Q
1 0 0  1
0 0 0  1
0 1 1  0
0 0 1  0
*/
