// Digital circuit muller-pipeline.dig as structural Verilog
module muller_pipeline (
  output c_1,
  output c_2,
  output c_3,
  output c_4
);

  wire not_1_out, not_2_out, not_3_out, not_4_out, or_1_out, reset_1_out;

  Reset #(.invertOutput("false")) reset_1 (.out(reset_1_out));
  or or_1 (or_1_out, c_4, reset_1_out);
  muller_c muller_c_1 (.A(not_1_out), .B(or_1_out), .rst(reset_1_out), .Y(c_1));
  not not_1 (not_1_out, c_2);
  not not_2 (not_2_out, c_3);
  muller_c muller_c_2 (.A(not_2_out), .B(c_1), .rst(reset_1_out), .Y(c_2));
  muller_c muller_c_3 (.A(not_3_out), .B(c_2), .rst(reset_1_out), .Y(c_3));
  not not_3 (not_3_out, c_4);
  muller_c muller_c_4 (.A(not_4_out), .B(c_3), .rst(reset_1_out), .Y(c_4));
  not not_4 (not_4_out, c_1);

  // Notes on the sheet:
  //   Run circuit in single gate step mode.
  //   {{de Starte die Schaltung im Gatterschrittmodus.}}
endmodule
