// Digital circuit multip_D_working_detail.dig as structural Verilog
module multip_D_working_detail (
  input  D,
  input  C,
  output D_2,
  output D_1,
  output D_0
);

  wire and_1_out, and_2_out, and_3_out, and_4_out, and_5_out, and_6_out, and_7_out, and_8_out, and_9_out,
       and_10_out, and_11_out, and_12_out, nor_1_out, nor_2_out, nor_4_out, nor_5_out, nor_6_out, nor_8_out,
       nor_9_out, nor_10_out, nor_12_out, not_1_out, not_2_out, not_3_out, not_4_out, not_5_out, not_6_out;

  and and_1 (and_1_out, D, C);
  not not_1 (not_1_out, D);
  and and_2 (and_2_out, C, not_1_out);
  not not_2 (not_2_out, C);
  nor nor_1 (nor_1_out, and_1_out, nor_2_out);
  nor nor_2 (nor_2_out, nor_1_out, and_2_out);
  and and_3 (and_3_out, nor_1_out, not_2_out);
  and and_4 (and_4_out, not_2_out, nor_2_out);
  nor nor_3 (D_0, and_3_out, nor_4_out);
  nor nor_4 (nor_4_out, D_0, and_4_out);
  and and_5 (and_5_out, D_0, C);
  not not_3 (not_3_out, D_0);
  and and_6 (and_6_out, C, not_3_out);
  not not_4 (not_4_out, C);
  nor nor_5 (nor_5_out, and_5_out, nor_6_out);
  nor nor_6 (nor_6_out, nor_5_out, and_6_out);
  and and_7 (and_7_out, nor_5_out, not_4_out);
  and and_8 (and_8_out, not_4_out, nor_6_out);
  nor nor_7 (D_1, and_7_out, nor_8_out);
  nor nor_8 (nor_8_out, D_1, and_8_out);
  and and_9 (and_9_out, D_1, C);
  not not_5 (not_5_out, D_1);
  and and_10 (and_10_out, C, not_5_out);
  not not_6 (not_6_out, C);
  nor nor_9 (nor_9_out, and_9_out, nor_10_out);
  nor nor_10 (nor_10_out, nor_9_out, and_10_out);
  and and_11 (and_11_out, nor_9_out, not_6_out);
  and and_12 (and_12_out, not_6_out, nor_10_out);
  nor nor_11 (D_2, and_11_out, nor_12_out);
  nor nor_12 (nor_12_out, D_2, and_12_out);
endmodule

/* Test case:
C D D_0 D_1 D_2
# clear all bits
C 0  0   x   x
C 0  0   0   x
C 0  0   0   0

# fill with one
C 1  1   0   0
C 1  1   1   0
C 1  1   1   1

# fill with zero
C 0  0   1   1
C 0  0   0   1
C 0  0   0   0
*/
