// Digital circuit counter2Bit3.dig as structural Verilog
module counter2Bit3 (
  input  C,
  output Q1,
  output Q0
);

  wire and_1_out, not_1_out, not_2_out;

  not not_1 (not_1_out, Q0);
  not not_2 (not_2_out, Q1);
  and and_1 (and_1_out, not_1_out, not_2_out);
  D_FF Q_1n (.D(Q0), .C(C), .Q(Q1));  // open: nQ
  D_FF Q_0n (.D(and_1_out), .C(C), .Q(Q0));  // open: nQ

  // Other names for the same wires on the sheet: Q_0n = Q0; Q_1n = Q1
endmodule
