// Digital circuit busTest.dig as structural Verilog
module busTest (
  input  [3:0] A,
  input  [3:0] B,
  output [3:0] S,
  output [3:0] U
);

  assign S = A ^ B;  // XOr xor_1, 4 bits wide
  assign U = ~(B ^ A);  // XNOr xnor_1, 4 bits wide

  // Notes on the sheet:
  //   S: pin 9,10,11,12
  //   A: pin 1,2,3,4
  //   B: pin 5,6,7,8
  //   U: pin 13,14,15,16
endmodule
