// Digital circuit mid.dig as structural Verilog
module mid (
  input  A,
  input  B,
  output Y
);

  wire inner_1_y, not_1_out, not_2_out;

  not not_1 (not_1_out, A);
  not not_2 (not_2_out, B);
  inner inner_1 (.A(not_1_out), .B(not_2_out), .Y(inner_1_y));
  not not_3 (Y, inner_1_y);
endmodule
