// Digital circuit mid2.dig as structural Verilog
module mid2 (
  input  A,
  input  B,
  output Y
);

  wire inner2_1_y, not_1_out, not_2_out;

  not not_1 (not_1_out, A);
  not not_2 (not_2_out, B);
  inner2 inner2_1 (.A(not_1_out), .B(not_2_out), .Y(inner2_1_y));
  not not_3 (Y, inner2_1_y);
endmodule
