// Digital circuit midBit.dig as structural Verilog
module midBit (
  input  A,
  input  B,
  output Y
);

  wire innerbit_1_y, not_1_out, not_2_out;

  not not_1 (not_1_out, A);
  not not_2 (not_2_out, B);
  innerBit innerbit_1 (.A(not_1_out), .B(not_2_out), .Y(innerbit_1_y));
  not not_3 (Y, innerbit_1_y);
endmodule
