// Digital circuit circular.dig as structural Verilog
module circular (
  input  A,
  input  C,
  output X
);

  wire A_nq, B_nq, C_nq, Q_A, Q_B, xor_1_out, xor_2_out, xor_3_out;

  xor xor_1 (xor_1_out, A_nq, A);
  D_FF u_A (.D(xor_1_out), .C(C), .Q(Q_A), .nQ(A_nq));
  xor xor_2 (xor_2_out, B_nq, Q_A);
  D_FF B (.D(xor_2_out), .C(C), .Q(Q_B), .nQ(B_nq));
  xor xor_3 (xor_3_out, C_nq, Q_B);
  D_FF u_C (.D(xor_3_out), .C(C), .Q(X), .nQ(C_nq));
endmodule

/* Test case:
C A X
C 0 1
C 0 1
C 0 1
C 0 0
C 0 1
C 0 1
C 0 1
C 0 0
C 1 1
C 1 1
C 1 0
C 1 0
C 1 1
C 1 1
C 1 0
C 1 0
*/
