// Digital circuit naming.dig as structural Verilog
// Simple test circuit
// used to test comments.
module naming (
  input  S0,
  input  S1,
  output S2,
  output S3
);

  wire nor_1_out;

  nor nor_1 (nor_1_out, S0, S1);
  xor xor_1 (S2, S0, nor_1_out);
  xor xor_2 (S3, nor_1_out, S1);

  // Notes on the sheet:
  //   S2: first output
  //   S0: First input
  //   This is a far longer text.
  //   S1: Second input
  //   S3: second output
  //   also with a longer text
endmodule

/* Test case:
S0 S1 S2 S3
0  0  1  1
0  1  0  1
1  0  1  0
1  1  1  1
*/
