// Digital circuit 08_twoFastClocks.dig as structural Verilog
module _08_twoFastClocks (
  input  clk,
  input  clk_2,
  output out_1
);

  and and_1 (out_1, clk, clk_2);

  // Notes on the sheet:
  //   clk: Hz: 500000
  //   clk_2: Hz: 500000
  //   Must generate an error as 
  //   two fast clocks are used.
endmodule
