// Digital circuit 14_inputInvert.dig as structural Verilog
module _14_inputInvert (
  input  A,
  input  B,
  output Y
);

  buf and_1 (Y, A);  // And open: In_2
endmodule

/* Test case:
A B Y
0 0 0
0 1 0
1 0 1
1 1 0
*/
