// Digital circuit probe.dig as structural Verilog
module probe (
  input  A,
  input  B,
  output Y
);

  wire not_1_out, Probe1_y, Probe2_y;

  not not_1 (not_1_out, B);
  pr1 Probe1 (.A(A), .B(B), .Y(Probe1_y));
  pr1 Probe2 (.A(A), .B(not_1_out), .Y(Probe2_y));
  xor xor_1 (Y, Probe1_y, Probe2_y);
endmodule
