// Digital circuit Adder.dig as structural Verilog
module Adder (
  input  A,
  input  B,
  input  c_i,
  output S,
  output c_o
);

  wire and_1_out, and_2_out, xor_1_out;

  xor xor_1 (xor_1_out, A, B);
  and and_1 (and_1_out, A, B);
  xor xor_2 (S, c_i, xor_1_out);
  and and_2 (and_2_out, c_i, xor_1_out);
  or or_1 (c_o, and_2_out, and_1_out);

  // Notes on the sheet:
  //   c_i: carry in
  //   S: sum
  //   c_o: carry out
endmodule

/* Test case:
A B c_i c_o S
loop (a,2)
loop (b,2)
loop (c,2)
(a) (b) (c) bits(2,a+b+c)
end loop
end loop
end loop
*/
