// Digital circuit doubleTest.dig as structural Verilog
module doubleTest (
  input  A,
  input  B,
  output Y1,
  output Y2
);

  wire double_1_p3, double_1_p4, double_1_p5, double_1_p6;

  // double double_1: pin names not known; wires that end beside it: A, B, double_1_p3, double_1_p4, double_1_p5, double_1_p6
  xor xor_1 (Y1, double_1_p3, double_1_p4);
  xnor xnor_1 (Y2, double_1_p5, double_1_p6);
endmodule

/* Test case:
A B Y1 Y2
0 0 0  1
0 1 1  0
1 0 1  0
1 1 0  1
*/
