// Digital circuit transtest.dig as structural Verilog
module transtest (
  input  A,
  input  B,
  output Y
);

  wire trans_1_p3, trans_1_p4;

  // trans trans_1: pin names not known; wires that end beside it: A, B, trans_1_p3, trans_1_p4
  xor xor_1 (Y, trans_1_p3, trans_1_p4);
endmodule

/* Test case:
A B Y
0 0 0
0 1 1
1 0 1
1 1 0
*/
