// Digital circuit debounce.dig as structural Verilog
module debounce (
  input  in,
  input  Clk,
  output out
);

  wire counter_1_ovf, d_ff_1_q, d_ff_2_q, xor_1_out;

  D_FF d_ff_1 (.D(in), .C(Clk), .Q(d_ff_1_q));  // open: nQ
  D_FF d_ff_2 (.D(d_ff_1_q), .C(Clk), .Q(d_ff_2_q));  // open: nQ
  xor xor_1 (xor_1_out, d_ff_2_q, d_ff_1_q);
  Register register_1 (.D(d_ff_2_q), .C(Clk), .en(counter_1_ovf), .Q(out));
  Counter #(.Bits(4)) counter_1 (.en(1'b1), .C(Clk), .clr(xor_1_out), .ovf(counter_1_ovf));  // open: out

  // Other names for the same wires on the sheet: C = Clk

  // Notes on the sheet:
  //   Clk: Hz: 10
endmodule

/* Test case:
           Clk in out
repeat(17)  C  1  x
            C  1  1

loop(n,32)  
            C  0  1
            C  1  1
end loop

repeat(17)  C  0  1
            C  0  0
*/
