// Digital circuit xorMulitInput.dig as structural Verilog
module xorMulitInput (
  input  A,
  input  B,
  input  C,
  output Y1,
  output Y2
);

  wire xor_1_out;

  xor xor_1 (xor_1_out, A, B);
  xor xor_2 (Y1, xor_1_out, C);
  xor xor_3 (Y2, C, B, A);
endmodule

/* Test case:
A  B  C Y1 Y2
0  0  0 0  0
0  0  1 1  1
0  1  0 1  1
0  1  1 0  0
1  0  0 1  1
1  0  1 0  0
1  1  0 0  0
1  1  1 1  1
 
*/
