// Digital circuit trafficLight.dig as structural Verilog
module trafficLight (
  input  Clock,
  output Red,
  output Yellow,
  output Green
);

  wire ms_jk_1_q, ms_jk_2_nq;

  MS_JK ms_jk_1 (.J(Yellow), .C(Clock), .K(Yellow), .Q(ms_jk_1_q), .nQ(Red));
  MS_JK ms_jk_2 (.J(1'b1), .C(Clock), .K(1'b1), .Q(Yellow), .nQ(ms_jk_2_nq));
  and and_1 (Green, ms_jk_1_q, ms_jk_2_nq);
endmodule
